// Logisim project Semester Proj.circ as structural Verilog: 6 circuits, main circuit main
module main (
);

  wire magnitude_comparator_1_a___b;
  wire [8:0] bit_extender_1_out, bit_extender_2_out, n8_bit_adder_1_p2;

  assign bit_extender_1_out = {{8{1'b0}}, 1'b1};  // Bit_Extender bit_extender_1
  assign bit_extender_2_out = {{8{1'b1}}, 1'b1};  // Bit_Extender bit_extender_2
  Magnitude_Comparator magnitude_comparator_1 (
    .A___B(magnitude_comparator_1_a___b), .A(bit_extender_1_out), .B(bit_extender_2_out));
  // _8_Bit_Adder 8_bit_adder_1: pin names not known; wires that end beside it: 8'hb7, n8_bit_adder_1_p2
  LED led_1 (.in(magnitude_comparator_1_a___b));
endmodule

module Magnitude_Comparator (
  input  [8:0] A,
  input  [8:0] B,
  output A___B
);

  wire and_1_out, and_2_out, and_3_out, and_4_out, and_5_out, and_6_out, and_7_out, and_8_out, and_9_out,
       and_10_out, and_11_out, and_12_out, and_13_out, and_14_out, and_15_out, and_16_out, and_17_out,
       and_18_out, and_19_out, and_20_out, and_21_out, and_22_out, and_23_out, and_24_out, and_25_out,
       and_26_out, and_27_out, and_28_out, and_29_out, and_30_out, and_31_out, and_32_out, and_33_out,
       and_34_out, nor_1_out, nor_2_out, nor_3_out, nor_4_out, nor_5_out, nor_6_out, nor_7_out, nor_8_out,
       nor_9_out, not_1_out, not_2_out, not_3_out, not_4_out, not_5_out, not_6_out, not_7_out, not_8_out,
       not_9_out, not_10_out, not_11_out, not_12_out, not_13_out, not_14_out, not_15_out, not_16_out,
       not_17_out, not_18_out, or_1_out, or_2_out;

  not not_1 (not_1_out, B[8]);
  not not_2 (not_2_out, A[8]);
  not not_3 (not_3_out, B[7]);
  not not_4 (not_4_out, A[7]);
  not not_5 (not_5_out, B[6]);
  not not_6 (not_6_out, A[6]);
  not not_7 (not_7_out, B[5]);
  not not_8 (not_8_out, A[5]);
  not not_9 (not_9_out, B[4]);
  not not_10 (not_10_out, A[4]);
  not not_11 (not_11_out, B[3]);
  not not_12 (not_12_out, A[3]);
  not not_13 (not_13_out, B[2]);
  not not_14 (not_14_out, A[2]);
  not not_15 (not_15_out, B[1]);
  not not_16 (not_16_out, A[1]);
  not not_17 (not_17_out, B[0]);
  not not_18 (not_18_out, A[0]);
  and and_1 (and_1_out, not_1_out, A[8]);
  and and_2 (and_2_out, B[8], not_2_out);
  and and_3 (and_3_out, not_3_out, A[7]);
  and and_4 (and_4_out, B[7], not_4_out);
  and and_5 (and_5_out, not_5_out, A[6]);
  and and_6 (and_6_out, B[6], not_6_out);
  and and_7 (and_7_out, not_7_out, A[5]);
  and and_8 (and_8_out, B[5], not_8_out);
  and and_9 (and_9_out, not_9_out, A[4]);
  and and_10 (and_10_out, B[4], not_10_out);
  and and_11 (and_11_out, not_11_out, A[3]);
  and and_12 (and_12_out, B[3], not_12_out);
  and and_13 (and_13_out, not_13_out, A[2]);
  and and_14 (and_14_out, B[2], not_14_out);
  and and_15 (and_15_out, not_15_out, A[1]);
  and and_16 (and_16_out, B[1], not_16_out);
  and and_17 (and_17_out, not_17_out, A[0]);
  and and_18 (and_18_out, B[0], not_18_out);
  nor nor_1 (nor_1_out, and_1_out, and_2_out);
  nor nor_2 (nor_2_out, and_3_out, and_4_out);
  nor nor_3 (nor_3_out, and_5_out, and_6_out);
  nor nor_4 (nor_4_out, and_7_out, and_8_out);
  nor nor_5 (nor_5_out, and_9_out, and_10_out);
  nor nor_6 (nor_6_out, and_11_out, and_12_out);
  nor nor_7 (nor_7_out, and_13_out, and_14_out);
  nor nor_8 (nor_8_out, and_15_out, and_16_out);
  nor nor_9 (nor_9_out, and_17_out, and_18_out);
  and and_19 (and_19_out, nor_1_out, and_3_out);
  and and_20 (and_20_out, nor_1_out, nor_2_out, and_5_out);
  and and_21 (and_21_out, nor_1_out, nor_2_out, nor_3_out, and_7_out);
  and and_22 (and_22_out, nor_1_out, nor_2_out, nor_3_out, nor_4_out, and_9_out);
  and and_23 (and_23_out, nor_1_out, nor_2_out, nor_3_out, nor_4_out);
  and and_24 (and_24_out, nor_5_out, and_11_out);
  and and_25 (and_25_out, nor_1_out, nor_2_out, nor_3_out, nor_4_out);
  and and_26 (and_26_out, nor_5_out, nor_6_out, and_13_out);
  and and_27 (and_27_out, nor_1_out, nor_2_out, nor_3_out, nor_4_out);
  and and_28 (and_28_out, nor_5_out, nor_6_out, nor_7_out, and_15_out);
  and and_29 (and_29_out, nor_1_out, nor_2_out, nor_3_out, nor_4_out);
  and and_30 (and_30_out, nor_5_out, nor_6_out, nor_7_out, nor_8_out, and_17_out);
  and and_31 (and_31_out, and_23_out, and_24_out);
  and and_32 (and_32_out, and_25_out, and_26_out);
  and and_33 (and_33_out, and_27_out, and_28_out);
  and and_34 (and_34_out, and_29_out, and_30_out);
  or or_1 (or_1_out, and_1_out, and_19_out, and_20_out, and_21_out, and_22_out);
  or or_2 (or_2_out, and_31_out, and_32_out, and_33_out, and_34_out);
  or or_3 (A___B, or_1_out, or_2_out);
  // also tied to GND on the sheet: nor_9_out
endmodule

module Day_Time (
  input  Day_Time,
  input  Pedestrian,
  input  Emergency,
  input  [7:0] of_Cars_in_RL0,
  input  [7:0] of_Cars_in_LL0,
  input  [7:0] of_Cars_in_RL1,
  input  [7:0] of_Cars_in_LL1,
  input  [7:0] of_Cars_in_RL2,
  input  [7:0] of_Cars_in_LL2,
  input  [7:0] of_Cars_in_RL3,
  input  [7:0] of_Cars_in_LL3,
  input  Countdown,
  input  Timer_Max,
  input  Command_to_Load_Max,
  input  Reset_Timer
);

  wire and_1_out, and_2_out, and_3_out, decoder_1_out0, decoder_1_out1, decoder_1_out2, decoder_1_out3,
       magnitude_comparator_1_a___b, magnitude_comparator_2_a___b, magnitude_comparator_3_a___b, not_1_out,
       not_2_out, or_1_out;
  wire [1:0] High_Bit_2_q;
  wire [8:0] multiplexer_1_out, multiplexer_2_out, n8_bit_adder_1_out_3, n8_bit_adder_2_out_3,
       n8_bit_adder_3_out_3, n8_bit_adder_4_out_3;

  _8_Bit_Adder u_8_bit_adder_1 (.A(of_Cars_in_RL0), .B(of_Cars_in_LL0), .out_3(n8_bit_adder_1_out_3));
  _8_Bit_Adder u_8_bit_adder_2 (.A(of_Cars_in_RL1), .B(of_Cars_in_LL1), .out_3(n8_bit_adder_2_out_3));
  _8_Bit_Adder u_8_bit_adder_3 (.A(of_Cars_in_RL2), .B(of_Cars_in_LL2), .out_3(n8_bit_adder_3_out_3));
  _8_Bit_Adder u_8_bit_adder_4 (.A(of_Cars_in_RL3), .B(of_Cars_in_LL3), .out_3(n8_bit_adder_4_out_3));
  and and_1 (and_1_out, Day_Time, ~Pedestrian, ~Emergency);  // AND_Gate
  Magnitude_Comparator magnitude_comparator_1 (
    .A___B(magnitude_comparator_1_a___b), .A(n8_bit_adder_1_out_3), .B(n8_bit_adder_2_out_3));
  Magnitude_Comparator magnitude_comparator_2 (
    .A___B(magnitude_comparator_2_a___b), .A(n8_bit_adder_3_out_3), .B(n8_bit_adder_4_out_3));
  Multiplexer #(.width(9), .enable("false")) multiplexer_1 (
    .in0(n8_bit_adder_2_out_3), .in1(n8_bit_adder_1_out_3), .out(multiplexer_1_out),
    .sel(magnitude_comparator_1_a___b));
  Multiplexer #(.width(9), .enable("false")) multiplexer_2 (
    .in0(n8_bit_adder_4_out_3), .in1(n8_bit_adder_3_out_3), .out(multiplexer_2_out),
    .sel(magnitude_comparator_2_a___b));
  Magnitude_Comparator magnitude_comparator_3 (
    .A___B(magnitude_comparator_3_a___b), .A(multiplexer_1_out), .B(multiplexer_2_out));
  and and_2 (and_2_out, ~magnitude_comparator_2_a___b, ~magnitude_comparator_3_a___b);  // AND_Gate
  and and_3 (and_3_out, ~magnitude_comparator_1_a___b, magnitude_comparator_3_a___b);  // AND_Gate
  not not_1 (not_1_out, magnitude_comparator_3_a___b);
  or or_1 (or_1_out, and_2_out, and_3_out);
  not not_2 (not_2_out, Countdown);
  D_Flip_Flop #(.trigger("high")) High_Bit (
    .clk(not_2_out), .D(not_1_out), .Q(High_Bit_2_q[1]));  // open: Qn, preset, en, reset
  D_Flip_Flop #(.trigger("high")) High_Bit_2 (
    .clk(not_2_out), .D(or_1_out), .Q(High_Bit_2_q[0]));  // open: Qn, preset, en, reset
  Decoder #(.select(2), .enable("false")) decoder_1 (
    .out0(decoder_1_out0), .out1(decoder_1_out1), .out2(decoder_1_out2), .out3(decoder_1_out3),
    .sel(High_Bit_2_q));

  // Notes on the sheet:
  //   Inputs From Timer:
  //   Inputs from Outside System
  //   North Bound Lanes:
  //   West Bound Lanes:
  //   South Bound Lanes
  //   East Bounds Lanes
  //   Inputs from Timer
  //   Outputs to TImer
  //   Enable Line
  //   After adjacent lanes were added
  //   Lane_0 > Lane_1
  //   Lane_2 > Lane_3
  //   Max(Lane_0, Lane_1) > Max(Lane_2, Lane_3)
  //   High Bit
  //   Low Bit
endmodule

module Full_Adder (
  input  A,
  input  B,
  input  C_in,
  output S,
  output C_out
);

  wire and_1_out, and_2_out, xor_1_out;

  xor xor_1 (xor_1_out, A, B);
  and and_1 (and_1_out, A, B);
  xor xor_2 (S, xor_1_out, C_in);
  and and_2 (and_2_out, xor_1_out, C_in);
  or or_1 (C_out, and_2_out, and_1_out);
endmodule

module _8_Bit_Adder (
  input  [7:0] A,
  input  [7:0] B,
  output [8:0] out_3
);

  wire full_adder_1_c_out, full_adder_2_c_out, full_adder_3_c_out, full_adder_4_c_out, full_adder_5_c_out,
       full_adder_6_c_out, full_adder_7_c_out;

  Full_Adder full_adder_1 (.A(A[0]), .B(B[0]), .C_in(1'b0), .S(out_3[0]), .C_out(full_adder_1_c_out));
  Full_Adder full_adder_2 (.A(A[1]), .B(B[1]), .C_in(full_adder_1_c_out), .S(out_3[1]), .C_out(full_adder_2_c_out));
  Full_Adder full_adder_3 (.A(A[2]), .B(B[2]), .C_in(full_adder_2_c_out), .S(out_3[2]), .C_out(full_adder_3_c_out));
  Full_Adder full_adder_4 (.A(A[3]), .B(B[3]), .C_in(full_adder_3_c_out), .S(out_3[3]), .C_out(full_adder_4_c_out));
  Full_Adder full_adder_5 (.A(A[4]), .B(B[4]), .C_in(full_adder_4_c_out), .S(out_3[4]), .C_out(full_adder_5_c_out));
  Full_Adder full_adder_6 (.A(A[5]), .B(B[5]), .C_in(full_adder_5_c_out), .S(out_3[5]), .C_out(full_adder_6_c_out));
  Full_Adder full_adder_7 (.A(A[6]), .B(B[6]), .C_in(full_adder_6_c_out), .S(out_3[6]), .C_out(full_adder_7_c_out));
  Full_Adder full_adder_8 (.A(A[7]), .B(B[7]), .C_in(full_adder_7_c_out), .S(out_3[7]), .C_out(out_3[8]));
endmodule

module Test_Circuit (
);

  wire magnitude_comparator_1_a___b;
  wire [8:0] n8_bit_adder_1_p2;

  // _8_Bit_Adder 8_bit_adder_1: pin names not known; wires that end beside it: 8'hb7, n8_bit_adder_1_p2
  Magnitude_Comparator magnitude_comparator_1 (.A___B(magnitude_comparator_1_a___b), .A(9'hb7), .B(9'h7e));
  LED led_1 (.in(magnitude_comparator_1_a___b));
endmodule
